# Fritzing sketch hookup_diagram (saved by Fritzing 0.9.0b)
breadboards: 1

parts:
  BeagleBone1 = BeagleBone Black
  Part1 = Breakout Board for Electret Microphone
  R1 = Resistor [tolerance=±5% resistance=2.2k package=THT]

nets:
  N1: BeagleBone1.no_name_yet#1, R1.Pin_0
  N2: BeagleBone1.no_name_yet#32, Part1.AUD
  N3: BeagleBone1.no_name_yet#36, Part1.VCC
  N4: Part1.GND, R1.Pin_1

custom parts:
  BeagleBone Black: BeagleBone Black rev. A5B
